// Logisim project  Multiplexer 8X1.circ as structural Verilog: 2 circuits, main circuit main
module main (
  input  [7:0] in_1,
  input  S3,
  input  S2,
  input  S1,
  output X
);

  _8X1_Multiplexer u_8x1_multiplexer_1 (.ENTADA_DE_DADOS(in_1), .s3(S3), .s2(S2), .s1(S1), .X(X));
endmodule

module _8X1_Multiplexer (
  input  [7:0] ENTADA_DE_DADOS,
  input  s3,
  input  s2,
  input  s1,
  output X
);

  wire and_1_out, and_2_out, and_3_out, and_4_out, and_5_out, and_6_out, and_7_out, and_8_out, not_1_out,
       not_2_out, not_3_out;

  not not_1 (not_1_out, s3);
  not not_2 (not_2_out, s1);
  not not_3 (not_3_out, s2);
  and and_1 (and_1_out, ENTADA_DE_DADOS[0], not_1_out, not_3_out, not_2_out);
  and and_2 (and_2_out, ENTADA_DE_DADOS[1], not_1_out, not_3_out, s1);
  and and_3 (and_3_out, ENTADA_DE_DADOS[2], not_1_out, not_2_out, s2);
  and and_4 (and_4_out, ENTADA_DE_DADOS[3], not_1_out, s2, s1);
  and and_5 (and_5_out, ENTADA_DE_DADOS[4], not_3_out, not_2_out, s3);
  and and_6 (and_6_out, ENTADA_DE_DADOS[5], not_3_out, s3, s1);
  and and_7 (and_7_out, ENTADA_DE_DADOS[6], not_2_out, s3, s2);
  and and_8 (and_8_out, ENTADA_DE_DADOS[7], s1, s3, s2);
  or or_1 (X, and_1_out, and_2_out, and_3_out, and_4_out, and_5_out, and_6_out, and_7_out, and_8_out);
endmodule
