// Logisim project 25TTTT.circ as structural Verilog: 3 circuits, main circuit main
module main (
  input  F,
  input  E,
  input  D,
  input  C,
  input  B,
  input  A,
  input  _9,
  input  _8,
  input  _7,
  input  _6,
  input  _5,
  input  _4,
  input  _3,
  input  _2,
  input  _1,
  input  _0
);

  wire n7sg_1_a, n7sg_1_b, n7sg_1_c, n7sg_1_d, n7sg_1_e, n7sg_1_f, n7sg_1_g, tc_1_s1, tc_1_s2, tc_1_s3,
       tc_1_s4;

  TC tc_1 (
    .F(F), .E(E), .D(D), .C(C), .B(B), .A(A), ._9(_9), ._8(_8), ._7(_7), ._6(_6), ._5(_5), ._4(_4), ._3(_3),
    ._2(_2), ._1(_1), ._0(_0), .s1(tc_1_s1), .s2(tc_1_s2), .s3(tc_1_s3), .s4(tc_1_s4));
  _7SG u_7sg_1 (
    .B1(tc_1_s4), .B2(tc_1_s3), .B3(tc_1_s2), .B4(tc_1_s1), .A(n7sg_1_a), .B(n7sg_1_b), .C(n7sg_1_c),
    .D(n7sg_1_d), .E(n7sg_1_e), .F(n7sg_1_f), .G(n7sg_1_g));
  _7_Segment_Display u_7_segment_display_1 (
    .g(n7sg_1_g), .f(n7sg_1_f), .a(n7sg_1_a), .b(n7sg_1_b), .e(n7sg_1_e), .d(n7sg_1_d), .c(n7sg_1_c));  // open: dp
endmodule

module _7SG (
  input  B1,
  input  B2,
  input  B3,
  input  B4,
  output A,
  output B,
  output C,
  output D,
  output E,
  output F,
  output G
);

  wire and_1_out, and_2_out, and_3_out, and_4_out, and_5_out, and_6_out, and_7_out, and_8_out, and_9_out,
       and_10_out, and_11_out, and_12_out, and_13_out, and_14_out, and_15_out, and_16_out, and_17_out,
       and_18_out, and_19_out, and_20_out, and_21_out, and_22_out, and_23_out, and_24_out, and_25_out,
       and_26_out, and_27_out, and_28_out, and_29_out, and_30_out, and_31_out, and_32_out, and_33_out,
       and_34_out, and_35_out, not_1_out, not_2_out, not_3_out, not_4_out, not_5_out, not_6_out, not_7_out,
       not_8_out, not_9_out, not_10_out, not_11_out, not_12_out, not_13_out, not_14_out, not_15_out,
       not_16_out, not_17_out, not_18_out, not_19_out, not_20_out, not_21_out, not_22_out, not_23_out,
       not_24_out, not_25_out, not_26_out, not_27_out, not_28_out, not_29_out, not_30_out, not_31_out,
       not_32_out, not_33_out, not_34_out, not_35_out, not_36_out, not_37_out, not_38_out, not_39_out,
       not_40_out, not_41_out, not_42_out, not_43_out;

  not not_1 (not_1_out, B2);
  and and_1 (and_1_out, not_1_out, not_2_out);
  not not_2 (not_2_out, B4);
  not not_3 (not_3_out, B1);
  and and_2 (and_2_out, not_3_out, B3);
  not not_4 (not_4_out, B1);
  and and_3 (and_3_out, not_4_out, B2, B4);
  and and_4 (and_4_out, B2, B3);
  and and_5 (and_5_out, B1, not_5_out, not_6_out);
  not not_5 (not_5_out, B2);
  not not_6 (not_6_out, B3);
  and and_6 (and_6_out, B1, not_7_out);
  not not_7 (not_7_out, B4);
  not not_8 (not_8_out, B1);
  and and_7 (and_7_out, not_8_out, not_9_out);
  not not_9 (not_9_out, B2);
  not not_10 (not_10_out, B1);
  and and_8 (and_8_out, not_10_out, not_11_out, not_12_out);
  not not_11 (not_11_out, B3);
  not not_12 (not_12_out, B4);
  not not_13 (not_13_out, B2);
  and and_9 (and_9_out, not_13_out, not_14_out);
  not not_14 (not_14_out, B4);
  not not_15 (not_15_out, B1);
  and and_10 (and_10_out, not_15_out, B3, B4);
  and and_11 (and_11_out, B1, not_16_out, B4);
  not not_16 (not_16_out, B3);
  not not_17 (not_17_out, B1);
  and and_12 (and_12_out, not_17_out, not_18_out);
  not not_18 (not_18_out, B3);
  not not_19 (not_19_out, B1);
  and and_13 (and_13_out, not_19_out, B4);
  not not_20 (not_20_out, B3);
  and and_14 (and_14_out, not_20_out, B4);
  not not_21 (not_21_out, B1);
  and and_15 (and_15_out, not_21_out, B2);
  and and_16 (and_16_out, B1, not_22_out);
  not not_22 (not_22_out, B2);
  not not_23 (not_23_out, B1);
  and and_17 (and_17_out, not_23_out, not_24_out, not_25_out);
  not not_24 (not_24_out, B2);
  not not_25 (not_25_out, B4);
  not not_26 (not_26_out, B2);
  and and_18 (and_18_out, not_26_out, B3, B4);
  and and_19 (and_19_out, B2, not_27_out, B4);
  not not_27 (not_27_out, B3);
  and and_20 (and_20_out, B2, B3, not_28_out);
  not not_28 (not_28_out, B4);
  and and_21 (and_21_out, B1, not_29_out);
  not not_29 (not_29_out, B3);
  not not_30 (not_30_out, B2);
  and and_22 (and_22_out, not_30_out, not_31_out);
  not not_31 (not_31_out, B4);
  and and_23 (and_23_out, B3, not_32_out);
  not not_32 (not_32_out, B4);
  and and_24 (and_24_out, B1, B3);
  and and_25 (and_25_out, B1, B2);
  not not_33 (not_33_out, B3);
  and and_26 (and_26_out, not_33_out, not_34_out);
  not not_34 (not_34_out, B4);
  not not_35 (not_35_out, B1);
  and and_27 (and_27_out, not_35_out, B2, not_36_out);
  not not_36 (not_36_out, B3);
  and and_28 (and_28_out, B2, not_37_out);
  not not_37 (not_37_out, B4);
  and and_29 (and_29_out, B1, not_38_out);
  not not_38 (not_38_out, B2);
  and and_30 (and_30_out, B1, B3);
  not not_39 (not_39_out, B2);
  and and_31 (and_31_out, not_39_out, B3);
  and and_32 (and_32_out, B3, not_40_out);
  not not_40 (not_40_out, B4);
  not not_41 (not_41_out, B1);
  and and_33 (and_33_out, not_41_out, B2, not_42_out);
  not not_42 (not_42_out, B3);
  and and_34 (and_34_out, B1, not_43_out);
  not not_43 (not_43_out, B2);
  and and_35 (and_35_out, B1, B4);
  or or_1 (B, and_7_out, and_8_out, and_9_out, and_10_out, and_11_out);
  or or_2 (C, and_12_out, and_13_out, and_14_out, and_15_out, and_16_out);
  or or_3 (D, and_17_out, and_18_out, and_19_out, and_20_out, and_21_out);
  or or_4 (E, and_22_out, and_23_out, and_24_out, and_25_out);
  or or_5 (F, and_26_out, and_27_out, and_28_out, and_29_out, and_30_out);
  or or_6 (G, and_31_out, and_32_out, and_33_out, and_34_out, and_35_out);
  or or_7 (A, and_1_out, and_2_out, and_3_out, and_4_out, and_5_out, and_6_out);
endmodule

module TC (
  input  F,
  input  E,
  input  D,
  input  C,
  input  B,
  input  A,
  input  _9,
  input  _8,
  input  _7,
  input  _6,
  input  _5,
  input  _4,
  input  _3,
  input  _2,
  input  _1,
  input  _0,
  output s1,
  output s2,
  output s3,
  output s4
);

  or or_1 (s1, _1, _3, _5, _7, _9, B, D, F);
  or or_2 (s2, _2, _3, _6, _7, _4, A, B, E, F);
  or or_3 (s3, _5, _6, _7, C, D, E, F);
  or or_4 (s4, _8, _9, A, B, C, D, E, F);
endmodule
