// Logisim project Demultiplexadores 1.circ as structural Verilog: 2 circuits, main circuit main
module main (
  input  S4,
  input  S3,
  input  S2,
  input  S1,
  input  X,
  output [15:0] SAIDA_DE_DADOS
);

  DEX_16X1 dex_16x1_1 (.X(X), .S4(S4), .S3(S3), .S2(S2), .S1(S1), .SAIDA_DE_DADOS(SAIDA_DE_DADOS));

  // Notes on the sheet:
  //   DEMULTIPLEXADORE DE 16
endmodule

module DEX_16X1 (
  input  S4,
  input  S3,
  input  S2,
  input  S1,
  input  X,
  output [15:0] SAIDA_DE_DADOS
);

  and and_1 (SAIDA_DE_DADOS[0], ~S1, ~S2, ~S3, ~S4, X);  // AND_Gate
  and and_2 (SAIDA_DE_DADOS[1], S1, ~S2, ~S3, ~S4, X);  // AND_Gate
  and and_3 (SAIDA_DE_DADOS[2], ~S1, S2, ~S3, ~S4, X);  // AND_Gate
  and and_4 (SAIDA_DE_DADOS[3], S1, S2, ~S3, ~S4, X);  // AND_Gate
  and and_5 (SAIDA_DE_DADOS[4], ~S1, ~S2, S3, ~S4, X);  // AND_Gate
  and and_6 (SAIDA_DE_DADOS[5], S1, ~S2, S3, ~S4, X);  // AND_Gate
  and and_7 (SAIDA_DE_DADOS[6], ~S1, S2, S3, ~S4, X);  // AND_Gate
  and and_8 (SAIDA_DE_DADOS[7], S1, S2, S3, ~S4, X);  // AND_Gate
  and and_9 (SAIDA_DE_DADOS[8], ~S1, ~S2, ~S3, S4, X);  // AND_Gate
  and and_10 (SAIDA_DE_DADOS[9], S1, ~S2, ~S3, S4, X);  // AND_Gate
  and and_11 (SAIDA_DE_DADOS[10], S1, ~S2, S3, ~S4, X);  // AND_Gate
  and and_12 (SAIDA_DE_DADOS[11], S1, ~S2, S3, S4, X);  // AND_Gate
  and and_13 (SAIDA_DE_DADOS[12], ~S1, ~S2, S3, S4, X);  // AND_Gate
  and and_14 (SAIDA_DE_DADOS[13], S1, ~S2, S3, S4, X);  // AND_Gate
  and and_15 (SAIDA_DE_DADOS[14], ~S1, S2, S3, S4, X);  // AND_Gate
  and and_16 (SAIDA_DE_DADOS[15], S1, S2, S3, S4, X);
endmodule
