// Logisim project Demultiplexadores 2.circ as structural Verilog: 3 circuits, main circuit main
module main (
  input  _7,
  input  _6,
  input  _5,
  input  _4,
  input  _3,
  input  _2,
  input  _1,
  input  _0,
  input  X,
  output _0_2,
  output _1_2,
  output _2_2,
  output _3_2,
  output _4_2,
  output _5_2,
  output _6_2,
  output _7_2
);

  wire codificador_1_s1, codificador_1_s2, codificador_1_s3;

  CODIFICADOR codificador_1 (
    ._7(_7), ._6(_6), ._5(_5), ._4(_4), ._3(_3), ._2(_2), ._1(_1), ._0(_0), .S3(codificador_1_s3),
    .S2(codificador_1_s2), .S1(codificador_1_s1));
  Demultiplexadores_8X1 demultiplexadores_8x1_1 (
    .X(X), .S3(codificador_1_s3), .S2(codificador_1_s2), .S1(codificador_1_s1), ._0(_0_2), ._1(_1_2),
    ._2(_2_2), ._3(_3_2), ._4(_4_2), ._5(_5_2), ._6(_6_2), ._7(_7_2));

  // Notes on the sheet:
  //   CODIFICADORE
  //   DEMULTIPLEXADOR
endmodule

module Demultiplexadores_8X1 (
  input  S3,
  input  S2,
  input  S1,
  input  X,
  output _0,
  output _1,
  output _2,
  output _3,
  output _4,
  output _5,
  output _6,
  output _7
);

  and and_1 (_0, ~S1, ~S2, ~S3, X);  // AND_Gate
  and and_2 (_1, S1, ~S2, ~S3, X);  // AND_Gate
  and and_3 (_2, ~S1, S2, ~S3, X);  // AND_Gate
  and and_4 (_3, S1, S2, ~S3, X);  // AND_Gate
  and and_5 (_4, ~S1, ~S2, S3, X);  // AND_Gate
  and and_6 (_5, S1, ~S2, S3, X);  // AND_Gate
  and and_7 (_6, ~S1, S2, S3, X);  // AND_Gate
  and and_8 (_7, S1, S2, S3, X);
endmodule

module CODIFICADOR (
  input  _7,
  input  _6,
  input  _5,
  input  _4,
  input  _3,
  input  _2,
  input  _1,
  input  _0,
  output S3,
  output S2,
  output S1
);

  or or_1 (S3, _4, _5, _6, _7);
  or or_2 (S2, _2, _3, _6, _7);
  or or_3 (S1, _1, _3, _5, _7);
endmodule
