// Logisim project GRAY 8 BITS.circ as structural Verilog: 2 circuits, main circuit main
module main (
  input  [7:0] BINARIO,
  output [7:0] GRAY
);

  GRAY_8_BITS gray_8_bits_1 (.BINARIO(BINARIO), .GRAY(GRAY));

  // Notes on the sheet:
  //    GRAY 8 BITS
endmodule

module GRAY_8_BITS (
  input  [7:0] BINARIO,
  output [7:0] GRAY
);

  xor xor_1 (GRAY[0], BINARIO[0], BINARIO[1]);
  xor xor_2 (GRAY[1], BINARIO[1], BINARIO[2]);
  xor xor_3 (GRAY[2], BINARIO[2], BINARIO[3]);
  xor xor_4 (GRAY[3], BINARIO[3], BINARIO[4]);
  xor xor_5 (GRAY[4], BINARIO[4], BINARIO[5]);
  xor xor_6 (GRAY[5], BINARIO[5], BINARIO[6]);
  xor xor_7 (GRAY[6], BINARIO[6], BINARIO[7]);

  assign GRAY[7] = BINARIO[7];
endmodule
