// Logisim project MULTIPLEXADOR 2.circ as structural Verilog: 1 circuit, main circuit main
module main (
  input  A,
  input  B,
  input  X
);

  wire demultiplexer_1_out0, demultiplexer_1_out1, multiplexer_1_out;

  Multiplexer multiplexer_1 (.in0(A), .in1(B), .out(multiplexer_1_out), .sel(X));  // open: en
  Demultiplexer demultiplexer_1 (
    .out0(demultiplexer_1_out0), .out1(demultiplexer_1_out1), .in(multiplexer_1_out), .sel(X));  // open: en
  LED u_A (.in(demultiplexer_1_out0));
  LED u_B (.in(demultiplexer_1_out1));
endmodule
