// Logisim project SOMA.circ as structural Verilog: 1 circuit, main circuit main
module main (
  input  [3:0] A,
  input  [3:0] B,
  input  in_3,
  output A_B,
  output A_B_2,
  output A_B_3,
  output [3:0] out_7
);

  Comparator #(.width(4)) comparator_1 (.a(A), .b(B), .gt(A_B), .eq(A_B_2), .lt(A_B_3));
  Adder #(.width(4)) adder_1 (.a(A), .b(B), .out(out_7), .cout(in_3));  // open: cin
endmodule
