// Logisim project TT.circ as structural Verilog: 1 circuit, main circuit main
module main (
  input  RES,
  output out_2,
  output out_3,
  output out_4,
  output out_5,
  output out_6
);

  wire clock_1_out;

  Clock clock_1 (.out(clock_1_out));
  J_K_Flip_Flop j_k_ff_1 (.J(1'b1), .clk(clock_1_out), .K(1'b1), .Q(out_2), .reset(RES));  // open: Qn, preset, en
  J_K_Flip_Flop j_k_ff_2 (.J(1'b1), .clk(out_2), .K(1'b1), .Q(out_3), .reset(RES));  // open: Qn, preset, en
  J_K_Flip_Flop j_k_ff_3 (.J(1'b1), .clk(out_3), .K(1'b1), .Q(out_4), .reset(RES));  // open: Qn, preset, en
  J_K_Flip_Flop j_k_ff_4 (.J(1'b1), .clk(out_4), .K(1'b1), .Q(out_5), .reset(RES));  // open: Qn, preset, en
  J_K_Flip_Flop j_k_ff_5 (.J(1'b1), .clk(out_5), .K(1'b1), .Q(out_6), .reset(RES));  // open: Qn, preset, en
endmodule
