// Logisim project avaliação 3.circ as structural Verilog: 32 circuits, main circuit main
module main (
  input  Fixa,
  input  Ligar_ou_Desligar
);

  wire A_out, Apagar_out, B_out, C_out, clock_1_out, D_out, Delete_out, E_out, \Espaço_out , F_out, G_out,
       H_out, I_out, J_out, K_out, L_out, M_out, N_out, O_out, P_out, Q_out, R_out, S_out, T_out, U_out,
       V_out, W_out, X_out, Y_out, Z_out;
  wire [6:0] codificador_2_1_out_3, or_1_out, teclado_1_out_28;

  Button A (.out(A_out));
  Button C (.out(C_out));
  Button B (.out(B_out));
  Button E (.out(E_out));
  Button D (.out(D_out));
  Button G (.out(G_out));
  Button F (.out(F_out));
  Button H (.out(H_out));
  Button I (.out(I_out));
  Button J (.out(J_out));
  Button K (.out(K_out));
  Clock clock_1 (.out(clock_1_out));
  Button M (.out(M_out));
  Button L (.out(L_out));
  Teclado teclado_1 (
    .A(A_out), .B(B_out), .C(C_out), .D(D_out), .E(E_out), .F(F_out), .G(G_out), .H(H_out), .I(I_out),
    .J(J_out), .K(K_out), .L(L_out), .M(M_out), .N(N_out), .O(O_out), .P(P_out), .Q(Q_out), .R(R_out),
    .S(S_out), .T(T_out), .U(U_out), .V(V_out), .W(W_out), .X(X_out), .Y(Y_out), .Z(Z_out), .FIXA(Fixa),
    .out_28(teclado_1_out_28));
  TTY tty_1 (.data(or_1_out), .clk(clock_1_out), .we(Ligar_ou_Desligar), .clr(Delete_out));
  Button N (.out(N_out));
  Button O (.out(O_out));
  CODIFICADOR_2 codificador_2_1 (.\espoço (\Espaço_out ), .back_space(Apagar_out), .out_3(codificador_2_1_out_3));
  assign or_1_out = teclado_1_out_28 | codificador_2_1_out_3;  // OR_Gate or_1, 7 bits wide
  Button Q (.out(Q_out));
  Button P (.out(P_out));
  Button S (.out(S_out));
  Button R (.out(R_out));
  Button Delete (.out(Delete_out));
  Button U (.out(U_out));
  Button T (.out(T_out));
  Button V (.out(V_out));
  Button W (.out(W_out));
  Button Y (.out(Y_out));
  Button X (.out(X_out));
  Button Z (.out(Z_out));
  Button Apagar (.out(Apagar_out));
  Button \Espaço  (.out(\Espaço_out ));
endmodule

module A_a (
  input  A,
  input  a_2,
  output [6:0] out_3
);

  or or_1 (out_3[6], A, a_2);

  assign out_3[5:0] = {a_2, 4'b0000, out_3[6]};
endmodule

module B_b (
  input  B,
  input  b_2,
  output [6:0] out_3
);

  or or_1 (out_3[6], B, b_2);

  assign out_3[5:0] = {b_2, 3'b000, out_3[6], 1'b0};
endmodule

module C_c (
  input  C,
  input  c_2,
  output [6:0] out_3
);

  or or_1 (out_3[6], C, c_2);

  assign out_3[5:0] = {c_2, 3'b000, {2{out_3[6]}}};
endmodule

module D_d (
  input  D,
  input  d_2,
  output [6:0] out_3
);

  or or_1 (out_3[6], D, d_2);

  assign out_3[5:0] = {d_2, 2'b00, out_3[6], 2'b00};
endmodule

module E_e (
  input  E,
  input  e_2,
  output [6:0] out_3
);

  or or_1 (out_3[6], E, e_2);

  assign out_3[5:0] = {e_2, 2'b00, out_3[6], 1'b0, out_3[6]};
endmodule

module F_f (
  input  F,
  input  f_2,
  output [6:0] out_3
);

  or or_1 (out_3[6], F, f_2);

  assign out_3[5:0] = {f_2, 2'b00, {2{out_3[6]}}, 1'b0};
endmodule

module G_g (
  input  G,
  input  g_2,
  output [6:0] out_3
);

  or or_1 (out_3[6], G, g_2);

  assign out_3[5:0] = {g_2, 2'b00, {3{out_3[6]}}};
endmodule

module H_h (
  input  H,
  input  h_2,
  output [6:0] out_3
);

  or or_1 (out_3[6], H, h_2);

  assign out_3[5:0] = {h_2, 1'b0, out_3[6], 3'b000};
endmodule

module I_i (
  input  I,
  input  i_2,
  output [6:0] out_3
);

  or or_1 (out_3[6], I, i_2);

  assign out_3[5:0] = {i_2, 1'b0, out_3[6], 2'b00, out_3[6]};
endmodule

module J_j (
  input  J,
  input  j_2,
  output [6:0] out_3
);

  or or_1 (out_3[6], J, j_2);

  assign out_3[5:0] = {j_2, 1'b0, out_3[6], 1'b0, out_3[6], 1'b0};
endmodule

module K_k (
  input  K,
  input  k_2,
  output [6:0] out_3
);

  or or_1 (out_3[6], K, k_2);

  assign out_3[5:0] = {k_2, 1'b0, out_3[6], 1'b0, {2{out_3[6]}}};
endmodule

module L_l (
  input  L,
  input  l_2,
  output [6:0] out_3
);

  or or_1 (out_3[6], L, l_2);

  assign out_3[5:0] = {l_2, 1'b0, {2{out_3[6]}}, 2'b00};
endmodule

module M_m (
  input  M,
  input  m_2,
  output [6:0] out_3
);

  or or_1 (out_3[6], M, m_2);

  assign out_3[5:0] = {m_2, 1'b0, {2{out_3[6]}}, 1'b0, out_3[6]};
endmodule

module N_n (
  input  N,
  input  n_2,
  output [6:0] out_3
);

  or or_1 (out_3[6], N, n_2);

  assign out_3[5:0] = {n_2, 1'b0, {3{out_3[6]}}, 1'b0};
endmodule

module O_o (
  input  O,
  input  o_2,
  output [6:0] out_3
);

  or or_1 (out_3[6], O, o_2);

  assign out_3[5:0] = {o_2, 1'b0, {4{out_3[6]}}};
endmodule

module P_p (
  input  P,
  input  p_2,
  output [6:0] out_3
);

  or or_1 (out_3[6], P, p_2);

  assign out_3[5:0] = {p_2, out_3[6], 4'b0000};
endmodule

module Q_q (
  input  Q,
  input  q_2,
  output [6:0] out_3
);

  or or_1 (out_3[6], Q, q_2);

  assign out_3[5:0] = {q_2, out_3[6], 3'b000, out_3[6]};
endmodule

module R_r (
  input  R,
  input  r_2,
  output [6:0] out_3
);

  or or_1 (out_3[6], R, r_2);

  assign out_3[5:0] = {r_2, out_3[6], 2'b00, out_3[6], 1'b0};
endmodule

module S_s (
  input  S,
  input  s_2,
  output [6:0] out_3
);

  or or_1 (out_3[6], S, s_2);

  assign out_3[5:0] = {s_2, out_3[6], 2'b00, {2{out_3[6]}}};
endmodule

module T_t (
  input  T,
  input  t_2,
  output [6:0] out_3
);

  or or_1 (out_3[6], T, t_2);

  assign out_3[5:0] = {t_2, out_3[6], 1'b0, out_3[6], 2'b00};
endmodule

module U_u (
  input  U,
  input  u_2,
  output [6:0] out_3
);

  or or_1 (out_3[6], U, u_2);

  assign out_3[5:0] = {u_2, out_3[6], 1'b0, out_3[6], 1'b0, out_3[6]};
endmodule

module V_v (
  input  V,
  input  v_2,
  output [6:0] out_3
);

  or or_1 (out_3[6], V, v_2);

  assign out_3[5:0] = {v_2, out_3[6], 1'b0, {2{out_3[6]}}, 1'b0};
endmodule

module W_w (
  input  W,
  input  w_2,
  output [6:0] out_3
);

  or or_1 (out_3[6], W, w_2);

  assign out_3[5:0] = {w_2, out_3[6], 1'b0, {3{out_3[6]}}};
endmodule

module X_x (
  input  X,
  input  x_2,
  output [6:0] out_3
);

  or or_1 (out_3[6], X, x_2);

  assign out_3[5:0] = {x_2, {2{out_3[6]}}, 3'b000};
endmodule

module Y_y (
  input  Y,
  input  y_2,
  output [6:0] out_3
);

  or or_1 (out_3[6], Y, y_2);

  assign out_3[5:0] = {y_2, {2{out_3[6]}}, 2'b00, out_3[6]};
endmodule

module Z_z (
  input  Z,
  input  z_2,
  output [6:0] out_3
);

  or or_1 (out_3[6], Z, z_2);

  assign out_3[5:0] = {z_2, {2{out_3[6]}}, 1'b0, out_3[6], 1'b0};
endmodule

module codificadores (
  input  A,
  input  B,
  input  C,
  input  D,
  input  E,
  input  F,
  input  G,
  input  H,
  input  I,
  input  J,
  input  K,
  input  L,
  input  M,
  input  N,
  input  O,
  input  P,
  input  Q,
  input  R,
  input  S,
  input  T,
  input  U,
  input  V,
  input  W,
  input  X,
  input  Y,
  input  Z,
  output [4:0] out_27,
  output A_2,
  output B_2,
  output C_2,
  output D_2,
  output E_2,
  output F_2,
  output G_2,
  output H_2,
  output I_2,
  output J_2,
  output K_2,
  output L_2,
  output M_2,
  output N_2,
  output O_2,
  output P_2,
  output Q_2,
  output R_2,
  output S_2,
  output T_2,
  output U_2,
  output V_2,
  output W_2,
  output X_2,
  output Y_2,
  output Z_2
);

  or B5 (out_27[4], Q, R, S, T, U, V, W, X, Y, Z);
  or B4 (out_27[3], I, J, K, L, M, N, O, P, Y, Z);
  or B3 (out_27[2], E, F, G, H, M, N, O, P, U, V, W, X);
  or B2 (out_27[1], C, D, G, H, K, L, O, P, S, T, W, X);
  or B1 (out_27[0], B, D, F, H, J, L, N, P, R, T, V, X, Z);

  assign A_2 = A;
  assign B_2 = B;
  assign C_2 = C;
  assign D_2 = D;
  assign E_2 = E;
  assign F_2 = F;
  assign G_2 = G;
  assign H_2 = H;
  assign I_2 = I;
  assign J_2 = J;
  assign K_2 = K;
  assign L_2 = L;
  assign M_2 = M;
  assign N_2 = N;
  assign O_2 = O;
  assign P_2 = P;
  assign Q_2 = Q;
  assign R_2 = R;
  assign S_2 = S;
  assign T_2 = T;
  assign U_2 = U;
  assign V_2 = V;
  assign W_2 = W;
  assign X_2 = X;
  assign Y_2 = Y;
  assign Z_2 = Z;
endmodule

module Teclado (
  input  A,
  input  B,
  input  C,
  input  D,
  input  E,
  input  F,
  input  G,
  input  H,
  input  I,
  input  J,
  input  K,
  input  L,
  input  M,
  input  N,
  input  O,
  input  P,
  input  Q,
  input  R,
  input  S,
  input  T,
  input  U,
  input  V,
  input  W,
  input  X,
  input  Y,
  input  Z,
  input  FIXA,
  output [6:0] out_28
);

  wire codificadores_1_a_2, codificadores_1_b_2, codificadores_1_c_2, codificadores_1_d_2,
       codificadores_1_e_2, codificadores_1_f_2, codificadores_1_g_2, codificadores_1_h_2,
       codificadores_1_i_2, codificadores_1_j_2, codificadores_1_k_2, codificadores_1_l_2,
       codificadores_1_m_2, codificadores_1_n_2, codificadores_1_o_2, codificadores_1_p_2,
       codificadores_1_q_2, codificadores_1_r_2, codificadores_1_s_2, codificadores_1_t_2,
       codificadores_1_u_2, codificadores_1_v_2, codificadores_1_w_2, codificadores_1_x_2,
       codificadores_1_y_2, codificadores_1_z_2, demultiplexer_1_out0, demultiplexer_1_out1,
       demultiplexer_2_out0, demultiplexer_2_out1, demultiplexer_3_out0, demultiplexer_3_out1,
       demultiplexer_4_out0, demultiplexer_4_out1, demultiplexer_5_out0, demultiplexer_5_out1,
       demultiplexer_6_out0, demultiplexer_6_out1, demultiplexer_7_out0, demultiplexer_7_out1,
       demultiplexer_8_out0, demultiplexer_8_out1, demultiplexer_9_out0, demultiplexer_9_out1,
       demultiplexer_10_out0, demultiplexer_10_out1, demultiplexer_11_out0, demultiplexer_11_out1,
       demultiplexer_12_out0, demultiplexer_12_out1, demultiplexer_13_out0, demultiplexer_13_out1,
       demultiplexer_14_out0, demultiplexer_14_out1, demultiplexer_15_out0, demultiplexer_15_out1,
       demultiplexer_16_out0, demultiplexer_16_out1, demultiplexer_17_out0, demultiplexer_17_out1,
       demultiplexer_18_out0, demultiplexer_18_out1, demultiplexer_19_out0, demultiplexer_19_out1,
       demultiplexer_20_out0, demultiplexer_20_out1, demultiplexer_21_out0, demultiplexer_21_out1,
       demultiplexer_22_out0, demultiplexer_22_out1, demultiplexer_23_out0, demultiplexer_23_out1,
       demultiplexer_24_out0, demultiplexer_24_out1, demultiplexer_25_out0, demultiplexer_25_out1,
       demultiplexer_26_out0, demultiplexer_26_out1;
  wire [4:0] codificadores_1_out_27;
  wire [6:0] a_a_1_out_3, b_b_1_out_3, c_c_1_out_3, d_d_1_out_3, e_e_1_out_3, f_f_1_out_3, g_g_1_out_3,
       h_h_1_out_3, i_i_1_out_3, j_j_1_out_3, k_k_1_out_3, l_l_1_out_3, m_m_1_out_3, n_n_1_out_3,
       o_o_1_out_3, p_p_1_out_3, q_q_1_out_3, r_r_1_out_3, s_s_1_out_3, t_t_1_out_3, u_u_1_out_3,
       v_v_1_out_3, w_w_1_out_3, x_x_1_out_3, y_y_1_out_3, z_z_1_out_3;

  Demultiplexer demultiplexer_1 (
    .out0(demultiplexer_1_out0), .out1(demultiplexer_1_out1), .in(codificadores_1_a_2), .sel(FIXA));  // open: en
  A_a a_a_1 (.A(demultiplexer_1_out1), .a_2(demultiplexer_1_out0), .out_3(a_a_1_out_3));
  Demultiplexer demultiplexer_2 (
    .out0(demultiplexer_2_out0), .out1(demultiplexer_2_out1), .in(codificadores_1_b_2), .sel(FIXA));  // open: en
  B_b b_b_1 (.B(demultiplexer_2_out1), .b_2(demultiplexer_2_out0), .out_3(b_b_1_out_3));
  Demultiplexer demultiplexer_3 (
    .out0(demultiplexer_3_out0), .out1(demultiplexer_3_out1), .in(codificadores_1_c_2), .sel(FIXA));  // open: en
  C_c c_c_1 (.C(demultiplexer_3_out1), .c_2(demultiplexer_3_out0), .out_3(c_c_1_out_3));
  Demultiplexer demultiplexer_4 (
    .out0(demultiplexer_4_out0), .out1(demultiplexer_4_out1), .in(codificadores_1_d_2), .sel(FIXA));  // open: en
  Demultiplexer demultiplexer_5 (
    .out0(demultiplexer_5_out0), .out1(demultiplexer_5_out1), .in(codificadores_1_e_2), .sel(FIXA));  // open: en
  E_e e_e_1 (.E(demultiplexer_5_out1), .e_2(demultiplexer_5_out0), .out_3(e_e_1_out_3));
  D_d d_d_1 (.D(demultiplexer_4_out1), .d_2(demultiplexer_4_out0), .out_3(d_d_1_out_3));
  Demultiplexer demultiplexer_6 (
    .out0(demultiplexer_6_out0), .out1(demultiplexer_6_out1), .in(codificadores_1_f_2), .sel(FIXA));  // open: en
  F_f f_f_1 (.F(demultiplexer_6_out1), .f_2(demultiplexer_6_out0), .out_3(f_f_1_out_3));
  Demultiplexer demultiplexer_7 (
    .out0(demultiplexer_7_out0), .out1(demultiplexer_7_out1), .in(codificadores_1_g_2), .sel(FIXA));  // open: en
  G_g g_g_1 (.G(demultiplexer_7_out1), .g_2(demultiplexer_7_out0), .out_3(g_g_1_out_3));
  Demultiplexer demultiplexer_8 (
    .out0(demultiplexer_8_out0), .out1(demultiplexer_8_out1), .in(codificadores_1_h_2), .sel(FIXA));  // open: en
  H_h h_h_1 (.H(demultiplexer_8_out1), .h_2(demultiplexer_8_out0), .out_3(h_h_1_out_3));
  Demultiplexer demultiplexer_9 (
    .out0(demultiplexer_9_out0), .out1(demultiplexer_9_out1), .in(codificadores_1_i_2), .sel(FIXA));  // open: en
  I_i i_i_1 (.I(demultiplexer_9_out1), .i_2(demultiplexer_9_out0), .out_3(i_i_1_out_3));
  Demultiplexer demultiplexer_10 (
    .out0(demultiplexer_10_out0), .out1(demultiplexer_10_out1), .in(codificadores_1_j_2), .sel(FIXA));  // open: en
  J_j j_j_1 (.J(demultiplexer_10_out1), .j_2(demultiplexer_10_out0), .out_3(j_j_1_out_3));
  Demultiplexer demultiplexer_11 (
    .out0(demultiplexer_11_out0), .out1(demultiplexer_11_out1), .in(codificadores_1_k_2), .sel(FIXA));  // open: en
  K_k k_k_1 (.K(demultiplexer_11_out1), .k_2(demultiplexer_11_out0), .out_3(k_k_1_out_3));
  Demultiplexer demultiplexer_12 (
    .out0(demultiplexer_12_out0), .out1(demultiplexer_12_out1), .in(codificadores_1_m_2), .sel(FIXA));  // open: en
  Demultiplexer demultiplexer_13 (
    .out0(demultiplexer_13_out0), .out1(demultiplexer_13_out1), .in(codificadores_1_l_2), .sel(FIXA));  // open: en
  L_l l_l_1 (.L(demultiplexer_13_out1), .l_2(demultiplexer_13_out0), .out_3(l_l_1_out_3));
  M_m m_m_1 (.M(demultiplexer_12_out1), .m_2(demultiplexer_12_out0), .out_3(m_m_1_out_3));
  Multiplexer #(.select(5), .width(7)) multiplexer_1 (
    .in0(a_a_1_out_3), .in1(b_b_1_out_3), .in2(c_c_1_out_3), .in3(d_d_1_out_3), .in4(e_e_1_out_3),
    .in5(f_f_1_out_3), .in6(g_g_1_out_3), .in7(h_h_1_out_3), .in8(i_i_1_out_3), .in9(j_j_1_out_3),
    .in10(k_k_1_out_3), .in11(l_l_1_out_3), .in12(m_m_1_out_3), .in13(n_n_1_out_3), .in14(o_o_1_out_3),
    .in15(p_p_1_out_3), .in16(q_q_1_out_3), .in17(r_r_1_out_3), .in18(s_s_1_out_3), .in19(t_t_1_out_3),
    .in20(u_u_1_out_3), .in21(v_v_1_out_3), .in22(w_w_1_out_3), .in23(x_x_1_out_3), .in24(y_y_1_out_3),
    .in25(z_z_1_out_3), .out(out_28), .sel(codificadores_1_out_27));  // open: in26, in27, in28, in29, in30, in31, en
  Demultiplexer demultiplexer_14 (
    .out0(demultiplexer_14_out0), .out1(demultiplexer_14_out1), .in(codificadores_1_n_2), .sel(FIXA));  // open: en
  N_n n_n_1 (.N(demultiplexer_14_out1), .n_2(demultiplexer_14_out0), .out_3(n_n_1_out_3));
  Demultiplexer demultiplexer_15 (
    .out0(demultiplexer_15_out0), .out1(demultiplexer_15_out1), .in(codificadores_1_o_2), .sel(FIXA));  // open: en
  O_o o_o_1 (.O(demultiplexer_15_out1), .o_2(demultiplexer_15_out0), .out_3(o_o_1_out_3));
  codificadores codificadores_1 (
    .A(A), .B(B), .C(C), .D(D), .E(E), .F(F), .G(G), .H(H), .I(I), .J(J), .K(K), .L(L), .M(M), .N(N), .O(O),
    .P(P), .Q(Q), .R(R), .S(S), .T(T), .U(U), .V(V), .W(W), .X(X), .Y(Y), .Z(Z), .A_2(codificadores_1_a_2),
    .B_2(codificadores_1_b_2), .C_2(codificadores_1_c_2), .D_2(codificadores_1_d_2),
    .E_2(codificadores_1_e_2), .F_2(codificadores_1_f_2), .G_2(codificadores_1_g_2),
    .H_2(codificadores_1_h_2), .I_2(codificadores_1_i_2), .J_2(codificadores_1_j_2),
    .K_2(codificadores_1_k_2), .L_2(codificadores_1_l_2), .M_2(codificadores_1_m_2),
    .N_2(codificadores_1_n_2), .O_2(codificadores_1_o_2), .P_2(codificadores_1_p_2),
    .Q_2(codificadores_1_q_2), .R_2(codificadores_1_r_2), .S_2(codificadores_1_s_2),
    .T_2(codificadores_1_t_2), .U_2(codificadores_1_u_2), .V_2(codificadores_1_v_2),
    .W_2(codificadores_1_w_2), .X_2(codificadores_1_x_2), .Y_2(codificadores_1_y_2),
    .Z_2(codificadores_1_z_2), .out_27(codificadores_1_out_27));
  Demultiplexer demultiplexer_16 (
    .out0(demultiplexer_16_out0), .out1(demultiplexer_16_out1), .in(codificadores_1_p_2), .sel(FIXA));  // open: en
  P_p p_p_1 (.P(demultiplexer_16_out1), .p_2(demultiplexer_16_out0), .out_3(p_p_1_out_3));
  Demultiplexer demultiplexer_17 (
    .out0(demultiplexer_17_out0), .out1(demultiplexer_17_out1), .in(codificadores_1_q_2), .sel(FIXA));  // open: en
  Q_q q_q_1 (.Q(demultiplexer_17_out1), .q_2(demultiplexer_17_out0), .out_3(q_q_1_out_3));
  Demultiplexer demultiplexer_18 (
    .out0(demultiplexer_18_out0), .out1(demultiplexer_18_out1), .in(codificadores_1_r_2), .sel(FIXA));  // open: en
  R_r r_r_1 (.R(demultiplexer_18_out1), .r_2(demultiplexer_18_out0), .out_3(r_r_1_out_3));
  Demultiplexer demultiplexer_19 (
    .out0(demultiplexer_19_out0), .out1(demultiplexer_19_out1), .in(codificadores_1_s_2), .sel(FIXA));  // open: en
  S_s s_s_1 (.S(demultiplexer_19_out1), .s_2(demultiplexer_19_out0), .out_3(s_s_1_out_3));
  Demultiplexer demultiplexer_20 (
    .out0(demultiplexer_20_out0), .out1(demultiplexer_20_out1), .in(codificadores_1_t_2), .sel(FIXA));  // open: en
  Demultiplexer demultiplexer_21 (
    .out0(demultiplexer_21_out0), .out1(demultiplexer_21_out1), .in(codificadores_1_u_2), .sel(FIXA));  // open: en
  T_t t_t_1 (.T(demultiplexer_20_out1), .t_2(demultiplexer_20_out0), .out_3(t_t_1_out_3));
  U_u u_u_1 (.U(demultiplexer_21_out1), .u_2(demultiplexer_21_out0), .out_3(u_u_1_out_3));
  Demultiplexer demultiplexer_22 (
    .out0(demultiplexer_22_out0), .out1(demultiplexer_22_out1), .in(codificadores_1_v_2), .sel(FIXA));  // open: en
  V_v v_v_1 (.V(demultiplexer_22_out1), .v_2(demultiplexer_22_out0), .out_3(v_v_1_out_3));
  Demultiplexer demultiplexer_23 (
    .out0(demultiplexer_23_out0), .out1(demultiplexer_23_out1), .in(codificadores_1_w_2), .sel(FIXA));  // open: en
  W_w w_w_1 (.W(demultiplexer_23_out1), .w_2(demultiplexer_23_out0), .out_3(w_w_1_out_3));
  Demultiplexer demultiplexer_24 (
    .out0(demultiplexer_24_out0), .out1(demultiplexer_24_out1), .in(codificadores_1_x_2), .sel(FIXA));  // open: en
  X_x x_x_1 (.X(demultiplexer_24_out1), .x_2(demultiplexer_24_out0), .out_3(x_x_1_out_3));
  Demultiplexer demultiplexer_25 (
    .out0(demultiplexer_25_out0), .out1(demultiplexer_25_out1), .in(codificadores_1_y_2), .sel(FIXA));  // open: en
  Y_y y_y_1 (.Y(demultiplexer_25_out1), .y_2(demultiplexer_25_out0), .out_3(y_y_1_out_3));
  Demultiplexer demultiplexer_26 (
    .out0(demultiplexer_26_out0), .out1(demultiplexer_26_out1), .in(codificadores_1_z_2), .sel(FIXA));  // open: en
  Z_z z_z_1 (.Z(demultiplexer_26_out1), .z_2(demultiplexer_26_out0), .out_3(z_z_1_out_3));
endmodule

module \ESPAÇO  (
  input  in_1,
  output [6:0] out_2
);


  assign out_2 = {1'b0, in_1, {5{1'b0}}};
endmodule

module BackSpace (
  input  in_1,
  output [6:0] out_2
);


  assign out_2 = {3'b000, in_1, 3'b000};
endmodule

module CODIFICADOR_2 (
  input  \espoço ,
  input  back_space,
  output [6:0] out_3
);

  wire [6:0] backspace_1_out_2, \espaço_1_out_2 ;

  \ESPAÇO  \espaço_1  (.in_1(\espoço ), .out_2(\espaço_1_out_2 ));
  BackSpace backspace_1 (.in_1(back_space), .out_2(backspace_1_out_2));
  assign out_3 = \espaço_1_out_2  | backspace_1_out_2;  // OR_Gate or_1, 7 bits wide
endmodule
