// Logisim project avaliação-4.circ as structural Verilog: 10 circuits, main circuit  sistema de rastreamento
module sistema_de_rastreamento (
);

  wire and_1_out, and_2_out, and_3_out, \botão_1_1_d , \botão_1_1_l_d , \botão_2_1_l_2 , \botão_2_1_n_2 ,
       \botão_2_1_o_2 , \botão_2_1_s_2 , clock_1_out, clock_2_out, DELETAR_out, L_out, LIGAR_OU_DESLIGAR_out,
       N_out, not_1_out, O_out, S_out, \sistema_e_definição_das_variáveis_lógicas_1_alerta_ligado ,
       \sistema_e_definição_das_variáveis_lógicas_1_caminhão_ligado , somador_e_multiplexador_2_1_saida;
  wire [6:0] or_1_out, somador_e_multiplexador_1_1_out_3, somador_e_multiplexador_2_1_y,
       somador_e_multiplexador_3_1_z;

  Button N (.out(N_out));
  Button O (.out(O_out));
  Button S (.out(S_out));
  Button L (.out(L_out));
  \BOTÃO_2  \botão_2_1  (
    .O(O_out), .L(L_out), .N(N_out), .S(S_out), .O_2(\botão_2_1_o_2 ), .L_2(\botão_2_1_l_2 ),
    .N_2(\botão_2_1_n_2 ), .S_2(\botão_2_1_s_2 ));
  LED L_D (.in(and_2_out));
  Button LIGAR_OU_DESLIGAR (.out(LIGAR_OU_DESLIGAR_out));
  \BOTÃO_1  \botão_1_1  (
    .LIGAR_OU_DESLIGAR(LIGAR_OU_DESLIGAR_out), .DELETAR(DELETAR_out), .L_D(\botão_1_1_l_d ), .D(\botão_1_1_d ));
  Button DELETAR (.out(DELETAR_out));
  Clock clock_1 (.out(clock_1_out));
  LED Alerta (.in(and_1_out));
  and and_1 (and_1_out, clock_1_out, \sistema_e_definição_das_variáveis_lógicas_1_alerta_ligado );
  \Sistema_e_Definição_das_Variáveis_Lógicas  \sistema_e_definição_das_variáveis_lógicas_1  (
    .S(\botão_2_1_s_2 ), .N(\botão_2_1_n_2 ), .L(\botão_2_1_l_2 ), .O(\botão_2_1_o_2 ),
    .\CAMINHÃO_LIGADO (\sistema_e_definição_das_variáveis_lógicas_1_caminhão_ligado ),
    .ALERTA_LIGADO(\sistema_e_definição_das_variáveis_lógicas_1_alerta_ligado ));
  not not_1 (not_1_out, \sistema_e_definição_das_variáveis_lógicas_1_caminhão_ligado );
  and and_2 (and_2_out, \botão_1_1_l_d , \sistema_e_definição_das_variáveis_lógicas_1_caminhão_ligado );
  and and_3 (and_3_out, not_1_out, \sistema_e_definição_das_variáveis_lógicas_1_alerta_ligado );
  Somador_e_multiplexador_1 somador_e_multiplexador_1_1 (
    .clock(clock_1_out), .sinal_1(and_2_out), .out_3(somador_e_multiplexador_1_1_out_3));
  Somador_e_multiplexador_2 somador_e_multiplexador_2_1 (
    .clock(clock_1_out), .sinal_2(and_3_out), .Y(somador_e_multiplexador_2_1_y),
    .saida(somador_e_multiplexador_2_1_saida));
  Somador_e_multiplexador_3 somador_e_multiplexador_3_1 (
    .clock(clock_1_out), .sinal_3(somador_e_multiplexador_2_1_saida), .Z(somador_e_multiplexador_3_1_z));
  assign or_1_out = somador_e_multiplexador_1_1_out_3 | somador_e_multiplexador_2_1_y | somador_e_multiplexador_3_1_z;  // OR_Gate or_1, 7 bits wide
  TTY #(.rows(4), .cols(43)) tty_1 (.data(or_1_out), .clk(clock_2_out), .we(\botão_1_1_l_d ), .clr(\botão_1_1_d ));
  Clock clock_2 (.out(clock_2_out));

  // Notes on the sheet:
  //   GPS
  //   Um sistema de rastreamento de veiculo utiliza 4 coordenadas geográficas
  //   Painel LCD
endmodule

module \Sistema_e_Definição_das_Variáveis_Lógicas  (
  input  S,
  input  N,
  input  L,
  input  O,
  output \CAMINHÃO_LIGADO ,
  output ALERTA_LIGADO
);

  and and_1 (\CAMINHÃO_LIGADO , ~S, ~N, ~L, ~O);  // AND_Gate
  or Alerta (ALERTA_LIGADO, S, N, L, O);
endmodule

module Somador_e_multiplexador_1 (
  input  clock,
  input  sinal_1,
  output [6:0] out_3
);

  wire and_1_out, and_2_out, j_k_ff_1_q, j_k_ff_2_qn, j_k_ff_3_qn, j_k_ff_4_qn, j_k_ff_5_qn;
  wire [4:0] j_k_ff_2_q;
  wire [6:0] codificador_de_letras_1_1_a, codificador_de_letras_1_1_a_2, codificador_de_letras_1_1_a_3,
       codificador_de_letras_1_1_a_4, codificador_de_letras_1_1_c, codificador_de_letras_1_1_d,
       codificador_de_letras_1_1_e, codificador_de_letras_1_1_espaso, codificador_de_letras_1_1_espaso_2,
       codificador_de_letras_1_1_g, codificador_de_letras_1_1_h, codificador_de_letras_1_1_i,
       codificador_de_letras_1_1_i_2, codificador_de_letras_1_1_l, codificador_de_letras_1_1_m,
       codificador_de_letras_1_1_n, codificador_de_letras_1_1_o, codificador_de_letras_1_1_o_2,
       codificador_de_letras_1_1_s, codificador_de_letras_1_1_t;

  J_K_Flip_Flop j_k_ff_1 (
    .J(1'b1), .clk(sinal_1), .K(1'b1), .Q(j_k_ff_1_q), .reset(and_2_out));  // open: Qn, preset, en
  and and_1 (and_1_out, clock, j_k_ff_1_q);
  Codificador_de_letras_1 codificador_de_letras_1_1 (
    .C(codificador_de_letras_1_1_c), .a(codificador_de_letras_1_1_a), .m(codificador_de_letras_1_1_m),
    .i(codificador_de_letras_1_1_i), .n(codificador_de_letras_1_1_n), .h(codificador_de_letras_1_1_h),
    .a_2(codificador_de_letras_1_1_a_2), .o(codificador_de_letras_1_1_o),
    .espaso(codificador_de_letras_1_1_espaso), .e(codificador_de_letras_1_1_e),
    .s(codificador_de_letras_1_1_s), .t(codificador_de_letras_1_1_t), .a_3(codificador_de_letras_1_1_a_3),
    .espaso_2(codificador_de_letras_1_1_espaso_2), .l(codificador_de_letras_1_1_l),
    .i_2(codificador_de_letras_1_1_i_2), .g(codificador_de_letras_1_1_g),
    .a_4(codificador_de_letras_1_1_a_4), .d(codificador_de_letras_1_1_d), .o_2(codificador_de_letras_1_1_o_2));
  J_K_Flip_Flop j_k_ff_2 (
    .J(1'b1), .clk(and_1_out), .K(1'b1), .Q(j_k_ff_2_q[0]), .Qn(j_k_ff_2_qn), .reset(and_2_out));  // open: preset, en
  J_K_Flip_Flop j_k_ff_3 (
    .J(1'b1), .clk(j_k_ff_2_qn), .K(1'b1), .Q(j_k_ff_2_q[1]), .Qn(j_k_ff_3_qn), .reset(and_2_out));  // open: preset, en
  Multiplexer #(.select(5), .width(7)) multiplexer_1 (
    .in0({7{1'b0}}), .in1(codificador_de_letras_1_1_c), .in2(codificador_de_letras_1_1_a),
    .in3(codificador_de_letras_1_1_m), .in4(codificador_de_letras_1_1_i), .in5(codificador_de_letras_1_1_n),
    .in6(codificador_de_letras_1_1_h), .in7(codificador_de_letras_1_1_a_2),
    .in8(codificador_de_letras_1_1_o), .in9(codificador_de_letras_1_1_espaso),
    .in10(codificador_de_letras_1_1_e), .in11(codificador_de_letras_1_1_s),
    .in12(codificador_de_letras_1_1_t), .in13(codificador_de_letras_1_1_a_3),
    .in14(codificador_de_letras_1_1_espaso_2), .in15(codificador_de_letras_1_1_l),
    .in16(codificador_de_letras_1_1_i_2), .in17(codificador_de_letras_1_1_g),
    .in18(codificador_de_letras_1_1_a_4), .in19(codificador_de_letras_1_1_d),
    .in20(codificador_de_letras_1_1_o_2), .in21(7'b0001101), .out(out_3), .sel(j_k_ff_2_q));  // open: in22, in23, in24, in25, in26, in27, in28, in29, in30, in31, en
  J_K_Flip_Flop j_k_ff_4 (
    .J(1'b1), .clk(j_k_ff_3_qn), .K(1'b1), .Q(j_k_ff_2_q[2]), .Qn(j_k_ff_4_qn), .reset(and_2_out));  // open: preset, en
  J_K_Flip_Flop j_k_ff_5 (
    .J(1'b1), .clk(j_k_ff_4_qn), .K(1'b1), .Q(j_k_ff_2_q[3]), .Qn(j_k_ff_5_qn), .reset(and_2_out));  // open: preset, en
  and and_2 (and_2_out, j_k_ff_2_q[1], j_k_ff_2_q[2], j_k_ff_2_q[4]);
  J_K_Flip_Flop j_k_ff_6 (
    .J(1'b1), .clk(j_k_ff_5_qn), .K(1'b1), .Q(j_k_ff_2_q[4]), .reset(and_2_out));  // open: Qn, preset, en
endmodule

module Somador_e_multiplexador_2 (
  input  clock,
  input  sinal_2,
  output [6:0] Y,
  output saida
);

  wire and_1_out, j_k_ff_1_q, j_k_ff_2_qn, j_k_ff_3_qn, j_k_ff_4_qn, j_k_ff_5_qn;
  wire [4:0] j_k_ff_2_q;
  wire [6:0] codificador_de_letras_2_1_a, codificador_de_letras_2_1_a_2, codificador_de_letras_2_1_a_3,
       codificador_de_letras_2_1_c, codificador_de_letras_2_1_d, codificador_de_letras_2_1_d_2,
       codificador_de_letras_2_1_e, codificador_de_letras_2_1_espaso, codificador_de_letras_2_1_espaso_2,
       codificador_de_letras_2_1_espaso_3, codificador_de_letras_2_1_f, codificador_de_letras_2_1_g,
       codificador_de_letras_2_1_h, codificador_de_letras_2_1_i, codificador_de_letras_2_1_i_2,
       codificador_de_letras_2_1_i_3, codificador_de_letras_2_1_l, codificador_de_letras_2_1_m,
       codificador_de_letras_2_1_n, codificador_de_letras_2_1_o, codificador_de_letras_2_1_o_2,
       codificador_de_letras_2_1_o_3, codificador_de_letras_2_1_s;

  Codificador_de_letras_2 codificador_de_letras_2_1 (
    .C(codificador_de_letras_2_1_c), .a(codificador_de_letras_2_1_a), .m(codificador_de_letras_2_1_m),
    .i(codificador_de_letras_2_1_i), .n(codificador_de_letras_2_1_n), .h(codificador_de_letras_2_1_h),
    .a_2(codificador_de_letras_2_1_a_2), .o(codificador_de_letras_2_1_o),
    .espaso(codificador_de_letras_2_1_espaso), .f(codificador_de_letras_2_1_f),
    .o_2(codificador_de_letras_2_1_o_2), .i_2(codificador_de_letras_2_1_i_2),
    .espaso_2(codificador_de_letras_2_1_espaso_2), .d(codificador_de_letras_2_1_d),
    .e(codificador_de_letras_2_1_e), .s(codificador_de_letras_2_1_s), .l(codificador_de_letras_2_1_l),
    .i_3(codificador_de_letras_2_1_i_3), .g(codificador_de_letras_2_1_g),
    .a_3(codificador_de_letras_2_1_a_3), .d_2(codificador_de_letras_2_1_d_2),
    .o_3(codificador_de_letras_2_1_o_3), .espaso_3(codificador_de_letras_2_1_espaso_3));
  and and_1 (and_1_out, clock, j_k_ff_1_q);
  J_K_Flip_Flop j_k_ff_1 (.J(1'b1), .clk(sinal_2), .K(1'b1), .Q(j_k_ff_1_q), .reset(saida));  // open: Qn, preset, en
  Multiplexer #(.select(5), .width(7)) multiplexer_1 (
    .in0({7{1'b0}}), .in1(codificador_de_letras_2_1_c), .in2(codificador_de_letras_2_1_a),
    .in3(codificador_de_letras_2_1_m), .in4(codificador_de_letras_2_1_i), .in5(codificador_de_letras_2_1_n),
    .in6(codificador_de_letras_2_1_h), .in7(codificador_de_letras_2_1_a_2),
    .in8(codificador_de_letras_2_1_o), .in9(codificador_de_letras_2_1_espaso),
    .in10(codificador_de_letras_2_1_f), .in11(codificador_de_letras_2_1_o_2),
    .in12(codificador_de_letras_2_1_i_2), .in13(codificador_de_letras_2_1_espaso_2),
    .in14(codificador_de_letras_2_1_d), .in15(codificador_de_letras_2_1_e),
    .in16(codificador_de_letras_2_1_s), .in17(codificador_de_letras_2_1_l),
    .in18(codificador_de_letras_2_1_i_3), .in19(codificador_de_letras_2_1_g),
    .in20(codificador_de_letras_2_1_a_3), .in21(codificador_de_letras_2_1_d_2),
    .in22(codificador_de_letras_2_1_o_3), .in23(codificador_de_letras_2_1_espaso_3), .out(Y), .sel(j_k_ff_2_q));  // open: in24, in25, in26, in27, in28, in29, in30, in31, en
  J_K_Flip_Flop j_k_ff_2 (
    .J(1'b1), .clk(and_1_out), .K(1'b1), .Q(j_k_ff_2_q[0]), .Qn(j_k_ff_2_qn), .reset(saida));  // open: preset, en
  J_K_Flip_Flop j_k_ff_3 (
    .J(1'b1), .clk(j_k_ff_2_qn), .K(1'b1), .Q(j_k_ff_2_q[1]), .Qn(j_k_ff_3_qn), .reset(saida));  // open: preset, en
  J_K_Flip_Flop j_k_ff_4 (
    .J(1'b1), .clk(j_k_ff_3_qn), .K(1'b1), .Q(j_k_ff_2_q[2]), .Qn(j_k_ff_4_qn), .reset(saida));  // open: preset, en
  and and_2 (saida, j_k_ff_2_q[3], j_k_ff_2_q[4]);
  J_K_Flip_Flop j_k_ff_5 (
    .J(1'b1), .clk(j_k_ff_4_qn), .K(1'b1), .Q(j_k_ff_2_q[3]), .Qn(j_k_ff_5_qn), .reset(saida));  // open: preset, en
  J_K_Flip_Flop j_k_ff_6 (
    .J(1'b1), .clk(j_k_ff_5_qn), .K(1'b1), .Q(j_k_ff_2_q[4]), .reset(saida));  // open: Qn, preset, en
endmodule

module Somador_e_multiplexador_3 (
  input  clock,
  input  sinal_3,
  output [6:0] Z
);

  wire and_1_out, and_2_out, j_k_ff_1_q, j_k_ff_2_qn, j_k_ff_3_qn, j_k_ff_4_qn, j_k_ff_5_qn;
  wire [4:0] j_k_ff_2_q;
  wire [6:0] codificador_de_letras_3_1_a, codificador_de_letras_3_1_a_2, codificador_de_letras_3_1_a_3,
       codificador_de_letras_3_1_a_4, codificador_de_letras_3_1_a_5, codificador_de_letras_3_1_d,
       codificador_de_letras_3_1_e, codificador_de_letras_3_1_e_2, codificador_de_letras_3_1_espaso,
       codificador_de_letras_3_1_espaso_2, codificador_de_letras_3_1_espaso_3,
       codificador_de_letras_3_1_espaso_4, codificador_de_letras_3_1_espaso_5, codificador_de_letras_3_1_f,
       codificador_de_letras_3_1_i, codificador_de_letras_3_1_i_2, codificador_de_letras_3_1_j,
       codificador_de_letras_3_1_o, codificador_de_letras_3_1_o_2, codificador_de_letras_3_1_o_3,
       codificador_de_letras_3_1_p, codificador_de_letras_3_1_q, codificador_de_letras_3_1_r,
       codificador_de_letras_3_1_r_2, codificador_de_letras_3_1_r_3, codificador_de_letras_3_1_r_4,
       codificador_de_letras_3_1_s, codificador_de_letras_3_1_t, codificador_de_letras_3_1_t_2,
       codificador_de_letras_3_1_u, codificador_de_letras_3_1_u_2;

  Codificador_de_letras_3 codificador_de_letras_3_1 (
    .P(codificador_de_letras_3_1_p), .o(codificador_de_letras_3_1_o), .r(codificador_de_letras_3_1_r),
    .q(codificador_de_letras_3_1_q), .u(codificador_de_letras_3_1_u), .e(codificador_de_letras_3_1_e),
    .espaso(codificador_de_letras_3_1_espaso), .s(codificador_de_letras_3_1_s),
    .a(codificador_de_letras_3_1_a), .i(codificador_de_letras_3_1_i), .u_2(codificador_de_letras_3_1_u_2),
    .espaso_2(codificador_de_letras_3_1_espaso_2), .f(codificador_de_letras_3_1_f),
    .o_2(codificador_de_letras_3_1_o_2), .r_2(codificador_de_letras_3_1_r_2),
    .a_2(codificador_de_letras_3_1_a_2), .espaso_3(codificador_de_letras_3_1_espaso_3),
    .d(codificador_de_letras_3_1_d), .a_3(codificador_de_letras_3_1_a_3),
    .espaso_4(codificador_de_letras_3_1_espaso_4), .t(codificador_de_letras_3_1_t),
    .r_3(codificador_de_letras_3_1_r_3), .a_4(codificador_de_letras_3_1_a_4),
    .j(codificador_de_letras_3_1_j), .e_2(codificador_de_letras_3_1_e_2),
    .t_2(codificador_de_letras_3_1_t_2), .o_3(codificador_de_letras_3_1_o_3),
    .r_4(codificador_de_letras_3_1_r_4), .i_2(codificador_de_letras_3_1_i_2),
    .a_5(codificador_de_letras_3_1_a_5), .espaso_5(codificador_de_letras_3_1_espaso_5));
  and and_1 (and_1_out, clock, j_k_ff_1_q);
  J_K_Flip_Flop j_k_ff_1 (
    .J(1'b1), .clk(sinal_3), .K(1'b1), .Q(j_k_ff_1_q), .reset(and_2_out));  // open: Qn, preset, en
  Multiplexer #(.select(5), .width(7)) multiplexer_1 (
    .in0({7{1'b0}}), .in1(codificador_de_letras_3_1_p), .in2(codificador_de_letras_3_1_o),
    .in3(codificador_de_letras_3_1_r), .in4(codificador_de_letras_3_1_q), .in5(codificador_de_letras_3_1_u),
    .in6(codificador_de_letras_3_1_e), .in7(codificador_de_letras_3_1_espaso),
    .in8(codificador_de_letras_3_1_s), .in9(codificador_de_letras_3_1_a), .in10(codificador_de_letras_3_1_i),
    .in11(codificador_de_letras_3_1_u_2), .in12(codificador_de_letras_3_1_espaso_2),
    .in13(codificador_de_letras_3_1_f), .in14(codificador_de_letras_3_1_o_2),
    .in15(codificador_de_letras_3_1_r_2), .in16(codificador_de_letras_3_1_a_2),
    .in17(codificador_de_letras_3_1_espaso_3), .in18(codificador_de_letras_3_1_d),
    .in19(codificador_de_letras_3_1_a_3), .in20(codificador_de_letras_3_1_espaso_4),
    .in21(codificador_de_letras_3_1_t), .in22(codificador_de_letras_3_1_r_3),
    .in23(codificador_de_letras_3_1_a_4), .in24(codificador_de_letras_3_1_j),
    .in25(codificador_de_letras_3_1_e_2), .in26(codificador_de_letras_3_1_t_2),
    .in27(codificador_de_letras_3_1_o_3), .in28(codificador_de_letras_3_1_r_4),
    .in29(codificador_de_letras_3_1_i_2), .in30(codificador_de_letras_3_1_a_5),
    .in31(codificador_de_letras_3_1_espaso_5), .out(Z), .sel(j_k_ff_2_q));  // open: en
  J_K_Flip_Flop j_k_ff_2 (
    .J(1'b1), .clk(and_1_out), .K(1'b1), .Q(j_k_ff_2_q[0]), .Qn(j_k_ff_2_qn), .reset(and_2_out));  // open: preset, en
  J_K_Flip_Flop j_k_ff_3 (
    .J(1'b1), .clk(j_k_ff_2_qn), .K(1'b1), .Q(j_k_ff_2_q[1]), .Qn(j_k_ff_3_qn));  // open: preset, en, reset
  J_K_Flip_Flop j_k_ff_4 (
    .J(1'b1), .clk(j_k_ff_3_qn), .K(1'b1), .Q(j_k_ff_2_q[2]), .Qn(j_k_ff_4_qn));  // open: preset, en, reset
  and and_2 (and_2_out, j_k_ff_2_q[0], j_k_ff_2_q[1], j_k_ff_2_q[2], j_k_ff_2_q[3], j_k_ff_2_q[4]);
  J_K_Flip_Flop j_k_ff_5 (
    .J(1'b1), .clk(j_k_ff_4_qn), .K(1'b1), .Q(j_k_ff_2_q[3]), .Qn(j_k_ff_5_qn));  // open: preset, en, reset
  J_K_Flip_Flop j_k_ff_6 (.J(1'b1), .clk(j_k_ff_5_qn), .K(1'b1), .Q(j_k_ff_2_q[4]));  // open: Qn, preset, en, reset
endmodule

module Codificador_de_letras_1 (
  output [6:0] C,
  output [6:0] a,
  output [6:0] m,
  output [6:0] i,
  output [6:0] n,
  output [6:0] h,
  output [6:0] a_2,
  output [6:0] o,
  output [6:0] espaso,
  output [6:0] e,
  output [6:0] s,
  output [6:0] t,
  output [6:0] a_3,
  output [6:0] espaso_2,
  output [6:0] l,
  output [6:0] i_2,
  output [6:0] g,
  output [6:0] a_4,
  output [6:0] d,
  output [6:0] o_2
);


  assign a = 7'b1100001;
  assign a_2 = 7'b1100001;
  assign a_3 = 7'b1100001;
  assign a_4 = 7'b1100001;
  assign C = 7'b1000011;
  assign d = 7'b1100100;
  assign e = 7'b1100101;
  assign espaso = 7'b0100000;
  assign espaso_2 = 7'b0100000;
  assign g = 7'b1100111;
  assign h = 7'b1101000;
  assign i = 7'b1101001;
  assign i_2 = 7'b1101001;
  assign l = 7'b1101100;
  assign m = 7'b1101101;
  assign n = 7'b1101110;
  assign o = 7'b1101111;
  assign o_2 = 7'b1101111;
  assign s = 7'b1110011;
  assign t = 7'b1110100;
endmodule

module Codificador_de_letras_2 (
  output [6:0] C,
  output [6:0] a,
  output [6:0] m,
  output [6:0] i,
  output [6:0] n,
  output [6:0] h,
  output [6:0] a_2,
  output [6:0] o,
  output [6:0] espaso,
  output [6:0] f,
  output [6:0] o_2,
  output [6:0] i_2,
  output [6:0] espaso_2,
  output [6:0] d,
  output [6:0] e,
  output [6:0] s,
  output [6:0] l,
  output [6:0] i_3,
  output [6:0] g,
  output [6:0] a_3,
  output [6:0] d_2,
  output [6:0] o_3,
  output [6:0] espaso_3
);


  assign a = 7'b1100001;
  assign a_2 = 7'b1100001;
  assign a_3 = 7'b1100001;
  assign C = 7'b1000011;
  assign d = 7'b1100100;
  assign d_2 = 7'b1100100;
  assign e = 7'b1100101;
  assign espaso = 7'b0100000;
  assign espaso_2 = 7'b0100000;
  assign espaso_3 = 7'b0100000;
  assign f = 7'b1100110;
  assign g = 7'b1100111;
  assign h = 7'b1101000;
  assign i = 7'b1101001;
  assign i_2 = 7'b1101001;
  assign i_3 = 7'b1101001;
  assign l = 7'b1101100;
  assign m = 7'b1101101;
  assign n = 7'b1101110;
  assign o = 7'b1101111;
  assign o_2 = 7'b1101111;
  assign o_3 = 7'b1101111;
  assign s = 7'b1110011;
endmodule

module Codificador_de_letras_3 (
  output [6:0] P,
  output [6:0] o,
  output [6:0] r,
  output [6:0] q,
  output [6:0] u,
  output [6:0] e,
  output [6:0] espaso,
  output [6:0] s,
  output [6:0] a,
  output [6:0] i,
  output [6:0] u_2,
  output [6:0] espaso_2,
  output [6:0] f,
  output [6:0] o_2,
  output [6:0] r_2,
  output [6:0] a_2,
  output [6:0] espaso_3,
  output [6:0] d,
  output [6:0] a_3,
  output [6:0] espaso_4,
  output [6:0] t,
  output [6:0] r_3,
  output [6:0] a_4,
  output [6:0] j,
  output [6:0] e_2,
  output [6:0] t_2,
  output [6:0] o_3,
  output [6:0] r_4,
  output [6:0] i_2,
  output [6:0] a_5,
  output [6:0] espaso_5
);


  assign a = 7'b1100001;
  assign a_2 = 7'b1100001;
  assign a_3 = 7'b1100001;
  assign a_4 = 7'b1100001;
  assign a_5 = 7'b1100001;
  assign d = 7'b1100100;
  assign e = 7'b1100101;
  assign e_2 = 7'b1100101;
  assign espaso = 7'b0100000;
  assign espaso_2 = 7'b0100000;
  assign espaso_3 = 7'b0100000;
  assign espaso_4 = 7'b0100000;
  assign espaso_5 = 7'b0100000;
  assign f = 7'b1100110;
  assign i = 7'b1101001;
  assign i_2 = 7'b1101001;
  assign j = 7'b1101010;
  assign o = 7'b1101111;
  assign o_2 = 7'b1101111;
  assign o_3 = 7'b1101111;
  assign P = 7'b1010000;
  assign q = 7'b1110001;
  assign r = 7'b1110010;
  assign r_2 = 7'b1110010;
  assign r_3 = 7'b1110010;
  assign r_4 = 7'b1110010;
  assign s = 7'b1110011;
  assign t = 7'b1110100;
  assign t_2 = 7'b1110100;
  assign u = 7'b1110101;
  assign u_2 = 7'b1110101;
endmodule

module \BOTÃO_1  (
  input  LIGAR_OU_DESLIGAR,
  input  DELETAR,
  output L_D,
  output D
);

  J_K_Flip_Flop j_k_ff_1 (.J(1'b1), .clk(LIGAR_OU_DESLIGAR), .K(1'b1), .Q(L_D));  // open: Qn, preset, en, reset
  J_K_Flip_Flop j_k_ff_2 (.J(1'b1), .clk(DELETAR), .K(1'b1), .Q(D));  // open: Qn, preset, en, reset
endmodule

module \BOTÃO_2  (
  input  O,
  input  L,
  input  N,
  input  S,
  output O_2,
  output L_2,
  output N_2,
  output S_2
);

  J_K_Flip_Flop j_k_ff_1 (.J(1'b1), .clk(O), .K(1'b1), .Q(O_2));  // open: Qn, preset, en, reset
  J_K_Flip_Flop j_k_ff_2 (.J(1'b1), .clk(L), .K(1'b1), .Q(L_2));  // open: Qn, preset, en, reset
  J_K_Flip_Flop j_k_ff_3 (.J(1'b1), .clk(N), .K(1'b1), .Q(N_2));  // open: Qn, preset, en, reset
  J_K_Flip_Flop j_k_ff_4 (.J(1'b1), .clk(S), .K(1'b1), .Q(S_2));  // open: Qn, preset, en, reset
endmodule
