// Logisim project contador básico para 8 bits.circ as structural Verilog: 1 circuit, main circuit main
module main (
  input  RES,
  output B1,
  output B2,
  output B3,
  output B4,
  output B5,
  output B6,
  output B7,
  output B8
);

  wire clock_1_out, j_k_ff_1_qn, j_k_ff_2_qn, j_k_ff_3_qn, j_k_ff_4_qn, j_k_ff_5_qn, j_k_ff_6_qn, j_k_ff_7_qn;

  Clock clock_1 (.out(clock_1_out));
  J_K_Flip_Flop j_k_ff_1 (
    .J(1'b1), .clk(clock_1_out), .K(1'b1), .Q(B1), .Qn(j_k_ff_1_qn), .reset(RES));  // open: preset, en
  J_K_Flip_Flop j_k_ff_2 (
    .J(1'b1), .clk(j_k_ff_1_qn), .K(1'b1), .Q(B2), .Qn(j_k_ff_2_qn), .reset(RES));  // open: preset, en
  J_K_Flip_Flop j_k_ff_3 (
    .J(1'b1), .clk(j_k_ff_2_qn), .K(1'b1), .Q(B3), .Qn(j_k_ff_3_qn), .reset(RES));  // open: preset, en
  J_K_Flip_Flop j_k_ff_4 (
    .J(1'b1), .clk(j_k_ff_3_qn), .K(1'b1), .Q(B4), .Qn(j_k_ff_4_qn), .reset(RES));  // open: preset, en
  J_K_Flip_Flop j_k_ff_5 (
    .J(1'b1), .clk(j_k_ff_4_qn), .K(1'b1), .Q(B5), .Qn(j_k_ff_5_qn), .reset(RES));  // open: preset, en
  J_K_Flip_Flop j_k_ff_6 (
    .J(1'b1), .clk(j_k_ff_5_qn), .K(1'b1), .Q(B6), .Qn(j_k_ff_6_qn), .reset(RES));  // open: preset, en
  J_K_Flip_Flop j_k_ff_7 (
    .J(1'b1), .clk(j_k_ff_6_qn), .K(1'b1), .Q(B7), .Qn(j_k_ff_7_qn), .reset(RES));  // open: preset, en
  J_K_Flip_Flop j_k_ff_8 (.J(1'b1), .clk(j_k_ff_7_qn), .K(1'b1), .Q(B8), .reset(RES));  // open: Qn, preset, en
endmodule
