// Logisim project tttttt.circ as structural Verilog: 4 circuits, main circuit main
module main (
  input  in_1,
  input  in_2,
  output out_3,
  output out_4,
  output out_5,
  output out_6,
  output out_7,
  output out_8,
  output out_9,
  output out_10,
  output out_11
);

  wire clock_1_out, clock_2_out, con2_1_b1, con2_1_b2, con2_1_b3, con2_1_b4, con2_1_s, con_1_b1, con_1_b2,
       con_1_b3, con_1_b4, con_1_out_2, j_k_ff_2_qn, j_k_ff_3_qn, j_k_ff_5_qn, j_k_ff_7_qn, n7sg_1_a,
       n7sg_1_b, n7sg_1_c, n7sg_1_d, n7sg_1_e, n7sg_1_f, n7sg_1_g, n7sg_2_a, n7sg_2_b, n7sg_2_c, n7sg_2_d,
       n7sg_2_e, n7sg_2_f, n7sg_2_g;

  Clock clock_1 (.out(clock_1_out));
  Clock clock_2 (.out(clock_2_out));
  J_K_Flip_Flop j_k_ff_1 (.J(1'b1), .clk(clock_1_out), .K(1'b1), .Q(out_3), .reset(in_1));  // open: Qn, preset, en
  J_K_Flip_Flop j_k_ff_2 (
    .J(1'b1), .clk(clock_2_out), .K(1'b1), .Q(out_7), .Qn(j_k_ff_2_qn), .reset(in_2));  // open: preset, en
  J_K_Flip_Flop j_k_ff_3 (
    .J(1'b1), .clk(j_k_ff_2_qn), .K(1'b1), .Q(out_10), .Qn(j_k_ff_3_qn), .reset(in_2));  // open: preset, en
  J_K_Flip_Flop j_k_ff_4 (.J(1'b1), .clk(out_3), .K(1'b1), .Q(out_4), .reset(in_1));  // open: Qn, preset, en
  J_K_Flip_Flop j_k_ff_5 (
    .J(1'b1), .clk(j_k_ff_3_qn), .K(1'b1), .Q(out_11), .Qn(j_k_ff_5_qn), .reset(in_2));  // open: preset, en
  J_K_Flip_Flop j_k_ff_6 (.J(1'b1), .clk(out_4), .K(1'b1), .Q(out_5), .reset(in_1));  // open: Qn, preset, en
  J_K_Flip_Flop j_k_ff_7 (
    .J(1'b1), .clk(j_k_ff_5_qn), .K(1'b1), .Q(out_8), .Qn(j_k_ff_7_qn), .reset(in_2));  // open: preset, en
  J_K_Flip_Flop j_k_ff_8 (.J(1'b1), .clk(out_5), .K(1'b1), .Q(out_6), .reset(in_1));  // open: Qn, preset, en
  J_K_Flip_Flop j_k_ff_9 (.J(1'b1), .clk(j_k_ff_7_qn), .K(1'b1), .Q(out_9));  // open: Qn, preset, en, reset
  con2 con2_1 (.s(con2_1_s), .clock(con_1_out_2), .b1(con2_1_b1), .b2(con2_1_b2), .b3(con2_1_b3), .b4(con2_1_b4));
  _7sg u_7sg_1 (
    .b1(con2_1_b4), .b2(con2_1_b3), .b3(con2_1_b2), .b4(con2_1_b1), .a(n7sg_1_a), .b(n7sg_1_b), .c(n7sg_1_c),
    .d(n7sg_1_d), .e(n7sg_1_e), .f(n7sg_1_f), .g(n7sg_1_g));
  _7_Segment_Display u_7_segment_display_1 (
    .g(n7sg_1_g), .f(n7sg_1_f), .a(n7sg_1_a), .b(n7sg_1_b), .e(n7sg_1_e), .d(n7sg_1_d), .c(n7sg_1_c));  // open: dp
  con con_1 (.out_2(con_1_out_2), .in_1(con2_1_s), .B1(con_1_b1), .B2(con_1_b2), .B3(con_1_b3), .B4(con_1_b4));
  _7_Segment_Display u_7_segment_display_2 (
    .g(n7sg_2_g), .f(n7sg_2_f), .a(n7sg_2_a), .b(n7sg_2_b), .e(n7sg_2_e), .d(n7sg_2_d), .c(n7sg_2_c));  // open: dp
  _7sg u_7sg_2 (
    .b1(con_1_b4), .b2(con_1_b3), .b3(con_1_b2), .b4(con_1_b1), .a(n7sg_2_a), .b(n7sg_2_b), .c(n7sg_2_c),
    .d(n7sg_2_d), .e(n7sg_2_e), .f(n7sg_2_f), .g(n7sg_2_g));
endmodule

module _7sg (
  input  b1,
  input  b2,
  input  b3,
  input  b4,
  output a,
  output b,
  output c,
  output d,
  output e,
  output f,
  output g
);

  wire and_1_out, and_2_out, and_3_out, and_4_out, and_5_out, and_6_out, and_7_out, and_8_out, and_9_out,
       and_10_out, and_11_out, and_12_out, and_13_out, and_14_out, and_15_out, and_16_out, and_17_out,
       and_18_out, and_19_out, and_20_out, and_21_out, and_22_out, and_23_out, and_24_out, and_25_out,
       and_26_out, and_27_out, and_28_out, and_29_out, and_30_out, and_31_out, and_32_out, and_33_out,
       and_34_out, and_35_out, not_1_out, not_2_out, not_3_out, not_4_out, not_5_out, not_6_out, not_7_out,
       not_8_out, not_9_out, not_10_out, not_11_out, not_12_out, not_13_out, not_14_out, not_15_out,
       not_16_out, not_17_out, not_18_out, not_19_out, not_20_out, not_21_out, not_22_out, not_23_out,
       not_24_out, not_25_out, not_26_out, not_27_out, not_28_out, not_29_out, not_30_out, not_31_out,
       not_32_out, not_33_out, not_34_out, not_35_out, not_36_out, not_37_out, not_38_out, not_39_out,
       not_40_out, not_41_out, not_42_out, not_43_out;

  not not_1 (not_1_out, b2);
  and and_1 (and_1_out, not_1_out, not_2_out);
  not not_2 (not_2_out, b4);
  not not_3 (not_3_out, b1);
  and and_2 (and_2_out, not_3_out, b3);
  not not_4 (not_4_out, b1);
  and and_3 (and_3_out, not_4_out, b2, b4);
  and and_4 (and_4_out, b2, b3);
  not not_5 (not_5_out, b2);
  and and_5 (and_5_out, b1, not_5_out, not_6_out);
  not not_6 (not_6_out, b3);
  and and_6 (and_6_out, b1, not_7_out);
  not not_7 (not_7_out, b4);
  not not_8 (not_8_out, b1);
  and and_7 (and_7_out, not_8_out, not_9_out);
  not not_9 (not_9_out, b2);
  not not_10 (not_10_out, b1);
  and and_8 (and_8_out, not_10_out, not_11_out, not_12_out);
  not not_11 (not_11_out, b3);
  not not_12 (not_12_out, b4);
  not not_13 (not_13_out, b2);
  and and_9 (and_9_out, not_13_out, not_14_out);
  not not_14 (not_14_out, b4);
  not not_15 (not_15_out, b1);
  and and_10 (and_10_out, not_15_out, b3, b4);
  not not_16 (not_16_out, b3);
  and and_11 (and_11_out, b1, not_16_out, b4);
  not not_17 (not_17_out, b1);
  and and_12 (and_12_out, not_17_out, not_18_out);
  not not_18 (not_18_out, b3);
  not not_19 (not_19_out, b1);
  and and_13 (and_13_out, not_19_out, b4);
  not not_20 (not_20_out, b3);
  and and_14 (and_14_out, not_20_out, b4);
  not not_21 (not_21_out, b1);
  and and_15 (and_15_out, not_21_out, b2);
  and and_16 (and_16_out, b1, not_22_out);
  not not_22 (not_22_out, b2);
  not not_23 (not_23_out, b1);
  and and_17 (and_17_out, not_23_out, not_24_out, not_25_out);
  not not_24 (not_24_out, b2);
  not not_25 (not_25_out, b4);
  not not_26 (not_26_out, b2);
  and and_18 (and_18_out, not_26_out, b3, b4);
  not not_27 (not_27_out, b3);
  and and_19 (and_19_out, b2, not_27_out, b4);
  and and_20 (and_20_out, b2, b3, not_28_out);
  not not_28 (not_28_out, b4);
  and and_21 (and_21_out, b1, not_29_out);
  not not_29 (not_29_out, b3);
  not not_30 (not_30_out, b2);
  and and_22 (and_22_out, not_30_out, not_31_out);
  not not_31 (not_31_out, b4);
  and and_23 (and_23_out, b3, not_32_out);
  not not_32 (not_32_out, b4);
  and and_24 (and_24_out, b1, b3);
  and and_25 (and_25_out, b1, b2);
  not not_33 (not_33_out, b3);
  and and_26 (and_26_out, not_33_out, not_34_out);
  not not_34 (not_34_out, b4);
  not not_35 (not_35_out, b1);
  and and_27 (and_27_out, not_35_out, b2, not_36_out);
  not not_36 (not_36_out, b3);
  and and_28 (and_28_out, b2, not_37_out);
  not not_37 (not_37_out, b4);
  and and_29 (and_29_out, b1, not_38_out);
  not not_38 (not_38_out, b2);
  and and_30 (and_30_out, b1, b3);
  not not_39 (not_39_out, b2);
  and and_31 (and_31_out, not_39_out, b3);
  and and_32 (and_32_out, b3, not_40_out);
  not not_40 (not_40_out, b4);
  not not_41 (not_41_out, b1);
  and and_33 (and_33_out, not_41_out, b2, not_42_out);
  not not_42 (not_42_out, b3);
  and and_34 (and_34_out, b1, not_43_out);
  not not_43 (not_43_out, b2);
  and and_35 (and_35_out, b1, b4);
  or or_1 (b, and_7_out, and_8_out, and_9_out, and_10_out, and_11_out);
  or or_2 (c, and_12_out, and_13_out, and_14_out, and_15_out, and_16_out);
  or or_3 (d, and_17_out, and_18_out, and_19_out, and_20_out, and_21_out);
  or or_4 (e, and_22_out, and_23_out, and_24_out, and_25_out);
  or or_5 (f, and_26_out, and_27_out, and_28_out, and_29_out, and_30_out);
  or or_6 (g, and_31_out, and_32_out, and_33_out, and_34_out, and_35_out);
  or or_7 (a, and_1_out, and_2_out, and_3_out, and_4_out, and_5_out, and_6_out);
endmodule

// s2
module con (
  input  in_1,
  output out_2,
  output B1,
  output B2,
  output B3,
  output B4
);

  wire and_1_out, and_2_out, clock_1_out, j_k_ff_1_qn, j_k_ff_2_qn, j_k_ff_3_qn;

  or or_1 (out_2, and_2_out, and_1_out);
  Clock clock_1 (.out(clock_1_out));
  J_K_Flip_Flop j_k_ff_1 (
    .J(1'b1), .clk(clock_1_out), .K(1'b1), .Q(B1), .Qn(j_k_ff_1_qn), .reset(out_2));  // open: preset, en
  and and_1 (and_1_out, B4, B2);
  J_K_Flip_Flop j_k_ff_2 (
    .J(1'b1), .clk(j_k_ff_1_qn), .K(1'b1), .Q(B2), .Qn(j_k_ff_2_qn), .reset(out_2));  // open: preset, en
  J_K_Flip_Flop j_k_ff_3 (
    .J(1'b1), .clk(j_k_ff_2_qn), .K(1'b1), .Q(B3), .Qn(j_k_ff_3_qn), .reset(out_2));  // open: preset, en
  J_K_Flip_Flop j_k_ff_4 (.J(1'b1), .clk(j_k_ff_3_qn), .K(1'b1), .Q(B4), .reset(out_2));  // open: Qn, preset, en
  and and_2 (and_2_out, B1, in_1, B2);
endmodule

module con2 (
  input  clock,
  output s,
  output b1,
  output b2,
  output b3,
  output b4
);

  wire and_2_out, j_k_ff_1_qn;

  and and_1 (s, b2, ~b1);  // AND_Gate
  J_K_Flip_Flop j_k_ff_1 (
    .J(1'b1), .clk(clock), .K(1'b1), .Q(b1), .Qn(j_k_ff_1_qn), .reset(and_2_out));  // open: preset, en
  and and_2 (and_2_out, b2, b1);
  J_K_Flip_Flop j_k_ff_2 (.J(1'b1), .clk(j_k_ff_1_qn), .K(1'b1), .Q(b2), .reset(and_2_out));  // open: Qn, preset, en

  assign b3 = 1'b0;
  assign b4 = 1'b0;
endmodule
